// Logisim project LC-2200-16.circ as structural Verilog: 4 circuits, main circuit main
module main (
  output [15:0] Bus_Value
);

  wire Clear, Clock, comparator_1_eq, DrALU, DrMEM, DrOFF, DrPC, DrREG, LdA, LdB, LdIR, LdMAR, LdPC, LdZ,
       not_1_out, WrMEM, WrREG, Z;
  wire [1:0] FUNC, RegSel;
  wire [2:0] OpCode;
  wire [3:0] RegNo;
  wire [12:0] IR_q;
  wire [15:0] A_q, alu_1_output, B_q, MAR_q, PC_q, ram_1_data, registerfile_1_out;

  Clock clock_1 (.out(Clock));
  Button button_1 (.out(Clear));
  Register #(.width(16)) PC (.D(Bus_Value), .en(LdPC), .Q(PC_q), .clk(Clock), .clr(Clear));
  assign Bus_Value = DrPC ? PC_q : 16'bz;  // Controlled_Buffer controlled_buffer_1
  FiniteStateMachine finitestatemachine_1 (
    .Clock(Clock), .Z(Z), .OpCode(OpCode), .DrREG(DrREG), .DrMEM(DrMEM), .DrALU(DrALU), .DrPC(DrPC),
    .DrOFF(DrOFF), .LdPC(LdPC), .LdIR(LdIR), .LdMAR(LdMAR), .LdA(LdA), .LdB(LdB), .LdZ(LdZ), .WrREG(WrREG),
    .WrMEM(WrMEM), .RegSel(RegSel), .FUNC(FUNC));
  Register #(.width(16)) A (.D(Bus_Value), .en(LdA), .Q(A_q), .clk(Clock), .clr(Clear));
  Comparator #(.width(16)) comparator_1 (.a(Bus_Value), .b({16{1'b0}}), .eq(comparator_1_eq));  // open: gt, lt
  Register #(.width(16)) B (.D(Bus_Value), .en(LdB), .Q(B_q), .clk(Clock), .clr(Clear));
  ALU alu_1 (.FUNC(FUNC), .A(A_q), .B(B_q), .Output(alu_1_output));
  assign Bus_Value = DrALU ? alu_1_output : 16'bz;  // Controlled_Buffer controlled_buffer_2
  Register #(.width(1)) register_1 (.D(comparator_1_eq), .en(LdZ), .Q(Z), .clk(Clock), .clr(Clear));
  RegisterFile registerfile_1 (
    .RegSel(RegNo), .WrReg(WrREG), .DataIn(Bus_Value), .Clock(Clock), .ClearRegFile(Clear),
    .Out(registerfile_1_out));
  assign Bus_Value = DrREG ? registerfile_1_out : 16'bz;  // Controlled_Buffer controlled_buffer_3
  Register #(.width(16)) MAR (.D(Bus_Value), .en(LdMAR), .Q(MAR_q), .clk(Clock), .clr(Clear));
  RAM #(.addrWidth(16), .dataWidth(16), .bus("separate")) ram_1 (
    .addr(MAR_q), .din(Bus_Value), .data(ram_1_data), .str(WrMEM), .clk(Clock), .ld(not_1_out), .clr(Clear));  // open: sel
  not not_1 (not_1_out, WrMEM);
  assign Bus_Value = DrMEM ? ram_1_data : 16'bz;  // Controlled_Buffer controlled_buffer_4
  Register #(.width(16)) IR (.D(Bus_Value), .en(LdIR), .Q({OpCode, IR_q}), .clk(Clock), .clr(Clear));
  assign Bus_Value = DrOFF ? {{11{IR_q[5]}}, IR_q[4:0]} : 16'bz;  // Controlled_Buffer controlled_buffer_5
  Multiplexer #(.select(2), .width(4)) multiplexer_1 (
    .in0(IR_q[12:9]), .in1(IR_q[8:5]), .in2(IR_q[4:1]), .out(RegNo), .sel(RegSel));  // open: in3, en
endmodule

module ALU (
  input  [15:0] A,
  input  [15:0] B,
  input  [1:0] FUNC,
  output [15:0] Output
);

  wire [15:0] adder_1_out, adder_2_out, nand_1_out, subtractor_1_out;

  Adder #(.width(16)) adder_1 (.a(A), .b(B), .out(adder_1_out));  // open: cin, cout
  assign nand_1_out = ~(A & B);  // NAND_Gate nand_1, 16 bits wide
  Multiplexer #(.select(2), .width(16)) multiplexer_1 (
    .in0(adder_1_out), .in1(nand_1_out), .in2(subtractor_1_out), .in3(adder_2_out), .out(Output), .sel(FUNC));  // open: en
  Subtractor #(.width(16)) subtractor_1 (.a(A), .b(B), .out(subtractor_1_out));  // open: bin, bout
  Adder #(.width(16)) adder_2 (.a(A), .b(16'h1), .out(adder_2_out));  // open: cin, cout
endmodule

module RegisterFile (
  input  [3:0] RegSel,
  input  WrReg,
  input  [15:0] DataIn,
  input  Clock,
  input  ClearRegFile,
  output [15:0] Out
);

  wire and_1_out, and_2_out, and_3_out, and_4_out, and_5_out, and_6_out, and_7_out, and_8_out, and_9_out,
       and_10_out, and_11_out, and_12_out, and_13_out, and_14_out, and_15_out, decoder_1_out0,
       decoder_1_out1, decoder_1_out2, decoder_1_out3, decoder_1_out4, decoder_1_out5, decoder_1_out6,
       decoder_1_out7, decoder_1_out8, decoder_1_out9, decoder_1_out10, decoder_1_out11, decoder_1_out12,
       decoder_1_out13, decoder_1_out14, decoder_1_out15;
  wire [15:0] a0, a1, a2, at, fp, k0, ra, s0, s1, s2, sp, t0, t1, t2, v0, zero;

  Decoder #(.select(4)) decoder_1 (
    .out0(decoder_1_out0), .out1(decoder_1_out1), .out2(decoder_1_out2), .out3(decoder_1_out3),
    .out4(decoder_1_out4), .out5(decoder_1_out5), .out6(decoder_1_out6), .out7(decoder_1_out7),
    .out8(decoder_1_out8), .out9(decoder_1_out9), .out10(decoder_1_out10), .out11(decoder_1_out11),
    .out12(decoder_1_out12), .out13(decoder_1_out13), .out14(decoder_1_out14), .out15(decoder_1_out15),
    .sel(RegSel));  // open: en
  and and_1 (and_1_out, WrReg, decoder_1_out1);
  and and_2 (and_2_out, WrReg, decoder_1_out2);
  and and_3 (and_3_out, WrReg, decoder_1_out3);
  and and_4 (and_4_out, WrReg, decoder_1_out4);
  and and_5 (and_5_out, WrReg, decoder_1_out5);
  and and_6 (and_6_out, WrReg, decoder_1_out6);
  and and_7 (and_7_out, WrReg, decoder_1_out7);
  and and_8 (and_8_out, WrReg, decoder_1_out8);
  and and_9 (and_9_out, WrReg, decoder_1_out9);
  and and_10 (and_10_out, WrReg, decoder_1_out10);
  and and_11 (and_11_out, WrReg, decoder_1_out11);
  and and_12 (and_12_out, WrReg, decoder_1_out12);
  and and_13 (and_13_out, WrReg, decoder_1_out13);
  and and_14 (and_14_out, WrReg, decoder_1_out14);
  and and_15 (and_15_out, WrReg, decoder_1_out15);
  Register #(.width(16)) register_1 (.D(DataIn), .en(1'b0), .Q(zero), .clk(Clock), .clr(ClearRegFile));
  Register #(.width(16)) register_2 (.D(DataIn), .en(and_1_out), .Q(at), .clk(Clock), .clr(ClearRegFile));
  Register #(.width(16)) register_3 (.D(DataIn), .en(and_2_out), .Q(v0), .clk(Clock), .clr(ClearRegFile));
  Register #(.width(16)) register_4 (.D(DataIn), .en(and_3_out), .Q(a0), .clk(Clock), .clr(ClearRegFile));
  Register #(.width(16)) register_5 (.D(DataIn), .en(and_4_out), .Q(a1), .clk(Clock), .clr(ClearRegFile));
  Register #(.width(16)) register_6 (.D(DataIn), .en(and_5_out), .Q(a2), .clk(Clock), .clr(ClearRegFile));
  Register #(.width(16)) register_7 (.D(DataIn), .en(and_6_out), .Q(t0), .clk(Clock), .clr(ClearRegFile));
  Register #(.width(16)) register_8 (.D(DataIn), .en(and_7_out), .Q(t1), .clk(Clock), .clr(ClearRegFile));
  Register #(.width(16)) register_9 (.D(DataIn), .en(and_8_out), .Q(t2), .clk(Clock), .clr(ClearRegFile));
  Register #(.width(16)) register_10 (.D(DataIn), .en(and_9_out), .Q(s0), .clk(Clock), .clr(ClearRegFile));
  Register #(.width(16)) register_11 (.D(DataIn), .en(and_10_out), .Q(s1), .clk(Clock), .clr(ClearRegFile));
  Register #(.width(16)) register_12 (.D(DataIn), .en(and_11_out), .Q(s2), .clk(Clock), .clr(ClearRegFile));
  Register #(.width(16)) register_13 (.D(DataIn), .en(and_12_out), .Q(k0), .clk(Clock), .clr(ClearRegFile));
  Register #(.width(16)) register_14 (.D(DataIn), .en(and_13_out), .Q(sp), .clk(Clock), .clr(ClearRegFile));
  Register #(.width(16)) register_15 (.D(DataIn), .en(and_14_out), .Q(fp), .clk(Clock), .clr(ClearRegFile));
  Register #(.width(16)) register_16 (.D(DataIn), .en(and_15_out), .Q(ra), .clk(Clock), .clr(ClearRegFile));
  Multiplexer #(.select(4), .width(16)) multiplexer_1 (
    .in0(zero), .in1(at), .in2(v0), .in3(a0), .in4(a1), .in5(a2), .in6(t0), .in7(t1), .in8(t2), .in9(s0),
    .in10(s1), .in11(s2), .in12(k0), .in13(sp), .in14(fp), .in15(ra), .out(Out), .sel(RegSel));  // open: en

  // Other names for the same wires on the sheet: Clear = ClearRegFile; Din[15:0] = DataIn; En = WrReg
endmodule

module FiniteStateMachine (
  input  Clock,
  input  Z,
  input  [2:0] OpCode,
  output DrREG,
  output DrMEM,
  output DrALU,
  output DrPC,
  output DrOFF,
  output LdPC,
  output LdIR,
  output LdMAR,
  output LdA,
  output LdB,
  output LdZ,
  output WrREG,
  output WrMEM,
  output [1:0] RegSel,
  output [1:0] FUNC
);

  wire chkZ, OpTest;
  wire [5:0] multiplexer_1_out, register_1_q, rom_1_data, rom_2_data, rom_3_data;

  Register #(.width(6)) register_1 (.D(multiplexer_1_out), .en(Clock), .Q(register_1_q), .clk(Clock));  // open: clr
  Multiplexer #(.select(2), .width(6)) multiplexer_1 (
    .in0(rom_1_data), .in1(rom_2_data), .in2(rom_3_data), .out(multiplexer_1_out), .sel({chkZ, OpTest}));  // open: in3, en
  ROM #(.addrWidth(6), .dataWidth(25)) rom_1 (
    .addr(register_1_q),
    .data({chkZ, OpTest, FUNC, RegSel, WrMEM, WrREG, LdZ, LdB, LdA, LdMAR, LdIR, LdPC, DrOFF, DrPC, DrALU, DrMEM, DrREG, rom_1_data}));  // open: sel
  ROM #(.addrWidth(3), .dataWidth(6)) rom_2 (.addr(OpCode), .data(rom_2_data));  // open: sel
  ROM #(.addrWidth(2), .dataWidth(6)) rom_3 (.addr({1'b0, Z}), .data(rom_3_data));  // open: sel

  // Notes on the sheet:
  //   contents of rom_1 (hex, n*v repeats v):
  //   6201 600902 801080 84044 108045 20100 84047 108048 220100 8404a 840b 20100 8404d 840e 210f 20080
  //   84051 8412 2113 40040 4055 88056 410117 1000000 4219 841a 900 a021c 840 1d
  //   contents of rom_2 (hex, n*v repeats v):
  //   3 6 9 c 10 14 1b 1d
  //   contents of rom_3 (hex, n*v repeats v):
  //   0 18
endmodule
